# Fritzing sketch RPi - Comm (saved by Fritzing 0.9.4)
breadboards: 3

parts:
  LED1 = smd LED [color="Orange (620nm)" package="1206 [SMD]"]
  R3 = Resistor [tolerance=±5% resistance=220 package=THT]
  J1 = T Cobbler Plus
  Raspberry_Pi_3 = Raspberry Pi 4 [part_number=RPI-4-b]
  Mod1 = KY-008 Laser Transmitter Module [package="Breakout board"]
  Part1 = Adafruit TSL2591 High Dynamic Range Digital Light Sensor [part_number="Adafruit #1980"]
  Raspberry_Pi_4 = Raspberry Pi 4 [part_number=RPI-4-b]
  LED3 = smd LED [color="Infrared (940nm)" package="1206 [SMD]"]
  J2 = T Cobbler Plus
  Part2 = Adafruit TSL2591 High Dynamic Range Digital Light Sensor [part_number="Adafruit #1980"]
  R4 = Resistor [tolerance=±5% resistance=220 package=THT]
  Raspberry_Pi_5 = Raspberry Pi 4 [part_number=RPI-4-b]
  J3 = T Cobbler Plus
  Part3 = Adafruit TSL2591 High Dynamic Range Digital Light Sensor [part_number="Adafruit #1980"]

nets:
  N1: LED1.cathode, R3.Pin_0
  N2: LED1.anode, J1.#6
  N3: R3.Pin_1, J1.GND#8, Part1.GND
  N4: J1.SDA, Part1.SDA
  N5: J1.SCL, Part1.SCL
  N6: J1.3.3V#16, Part1.VCC
  3V3: J1.3.3V#41, J1.3.3V#57, Raspberry_Pi_3.3v3, Raspberry_Pi_3.3V3
  5V: J1.5V, Raspberry_Pi_3.5V
  N7: J1.GPIO_2, Raspberry_Pi_3.GPIO2
  N8: J1.GPIO_3, Raspberry_Pi_3.GPIO3
  N9: J1.GND#46, J1.GND#49, J1.GND#54, J1.GND#60, J1.GND#65, J1.GND#70, J1.GND#74, J1.GND#79, Raspberry_Pi_3.GND
  N10: J1.GPIO_4, Raspberry_Pi_3.GPIO4
  N11: J1.GPIO_14, Raspberry_Pi_3.GPIO14
  N12: J1.GPIO_15, Raspberry_Pi_3.GPIO15
  N13: J1.GPIO_17, Raspberry_Pi_3.GPIO17
  N14: J1.GPIO_18, Raspberry_Pi_3.GPIO18
  N15: J1.GPIO_27, Raspberry_Pi_3.GPIO27
  N16: J1.GPIO_22, Raspberry_Pi_3.GPIO22
  N17: J1.GPIO_23, Raspberry_Pi_3.GPIO23
  N18: J1.GPIO_24, Raspberry_Pi_3.GPIO24
  N19: J1.GPIO_10, Raspberry_Pi_3.GPIO10
  N20: J1.GPIO_9, Raspberry_Pi_3.GPIO9
  N21: J1.GPIO_25, Raspberry_Pi_3.GPIO25
  N22: J1.GPIO_11, Raspberry_Pi_3.GPIO11
  N23: J1.GPIO_8, Raspberry_Pi_3.GPIO8
  N24: J1.GPIO_7, Raspberry_Pi_3.GPIO7
  N25: J1.ID_SD, Raspberry_Pi_3.ID_SD
  N26: J1.ID_SC, Raspberry_Pi_3.ID_SC
  N27: J1.GPIO_5, Raspberry_Pi_3.GPIO5
  N28: J1.GPIO_6, Raspberry_Pi_3.GPIO6
  N29: J1.GPIO_12, Raspberry_Pi_3.GPIO12
  N30: J1.GPIO_13, Raspberry_Pi_3.GPIO13
  N31: J1.GPIO_19, Raspberry_Pi_3.GPIO19
  N32: J1.GPIO_16, Raspberry_Pi_3.GPIO16
  N33: J1.GPIO_26, Raspberry_Pi_3.GPIO26
  N34: J1.GPIO_20, Raspberry_Pi_3.GPIO20
  N35: J1.GPIO_21, Raspberry_Pi_3.GPIO21
  N36: Mod1.S, J3.#6
  N37: Mod1.-, J3.GND#8, Part3.GND
  3V3_2: Raspberry_Pi_4.3v3, Raspberry_Pi_4.3V3, J2.3.3V#41, J2.3.3V#57
  N38: Raspberry_Pi_4.GPIO2, J2.GPIO_2
  N39: Raspberry_Pi_4.GPIO3, J2.GPIO_3
  N40: Raspberry_Pi_4.GPIO4, J2.GPIO_4
  N41: Raspberry_Pi_4.GND, J2.GND#46, J2.GND#49, J2.GND#54, J2.GND#60, J2.GND#65, J2.GND#70, J2.GND#74, J2.GND#79
  N42: Raspberry_Pi_4.GPIO17, J2.GPIO_17
  N43: Raspberry_Pi_4.GPIO27, J2.GPIO_27
  N44: Raspberry_Pi_4.GPIO22, J2.GPIO_22
  N45: Raspberry_Pi_4.GPIO10, J2.GPIO_10
  N46: Raspberry_Pi_4.GPIO9, J2.GPIO_9
  N47: Raspberry_Pi_4.GPIO11, J2.GPIO_11
  N48: Raspberry_Pi_4.ID_SD, J2.ID_SD
  N49: Raspberry_Pi_4.GPIO5, J2.GPIO_5
  N50: Raspberry_Pi_4.GPIO6, J2.GPIO_6
  N51: Raspberry_Pi_4.GPIO13, J2.GPIO_13
  N52: Raspberry_Pi_4.GPIO19, J2.GPIO_19
  N53: Raspberry_Pi_4.GPIO26, J2.GPIO_26
  N54: Raspberry_Pi_4.GPIO21, J2.GPIO_21
  N55: Raspberry_Pi_4.GPIO20, J2.GPIO_20
  N56: Raspberry_Pi_4.GPIO16, J2.GPIO_16
  N57: Raspberry_Pi_4.GPIO12, J2.GPIO_12
  N58: Raspberry_Pi_4.ID_SC, J2.ID_SC
  N59: Raspberry_Pi_4.GPIO7, J2.GPIO_7
  N60: Raspberry_Pi_4.GPIO8, J2.GPIO_8
  N61: Raspberry_Pi_4.GPIO25, J2.GPIO_25
  N62: Raspberry_Pi_4.GPIO24, J2.GPIO_24
  N63: Raspberry_Pi_4.GPIO23, J2.GPIO_23
  N64: Raspberry_Pi_4.GPIO18, J2.GPIO_18
  N65: Raspberry_Pi_4.GPIO15, J2.GPIO_15
  N66: Raspberry_Pi_4.GPIO14, J2.GPIO_14
  5V_2: Raspberry_Pi_4.5V, J2.5V
  N67: LED3.cathode, R4.Pin_0
  N68: LED3.anode, J2.#6
  N69: J2.SDA, Part2.SDA
  N70: J2.SCL, Part2.SCL
  N71: J2.GND#8, Part2.GND, R4.Pin_1
  N72: J2.3.3V#16, Part2.VCC
  3V3_3: Raspberry_Pi_5.3v3, Raspberry_Pi_5.3V3, J3.3.3V#41, J3.3.3V#57
  N73: Raspberry_Pi_5.GPIO2, J3.GPIO_2
  N74: Raspberry_Pi_5.GPIO3, J3.GPIO_3
  N75: Raspberry_Pi_5.GPIO4, J3.GPIO_4
  N76: Raspberry_Pi_5.GND, J3.GND#46, J3.GND#49, J3.GND#54, J3.GND#60, J3.GND#65, J3.GND#70, J3.GND#74, J3.GND#79
  N77: Raspberry_Pi_5.GPIO17, J3.GPIO_17
  N78: Raspberry_Pi_5.GPIO27, J3.GPIO_27
  N79: Raspberry_Pi_5.GPIO22, J3.GPIO_22
  N80: Raspberry_Pi_5.GPIO10, J3.GPIO_10
  N81: Raspberry_Pi_5.GPIO9, J3.GPIO_9
  N82: Raspberry_Pi_5.GPIO11, J3.GPIO_11
  N83: Raspberry_Pi_5.ID_SD, J3.ID_SD
  N84: Raspberry_Pi_5.GPIO5, J3.GPIO_5
  N85: Raspberry_Pi_5.GPIO6, J3.GPIO_6
  N86: Raspberry_Pi_5.GPIO13, J3.GPIO_13
  N87: Raspberry_Pi_5.GPIO19, J3.GPIO_19
  N88: Raspberry_Pi_5.GPIO26, J3.GPIO_26
  N89: Raspberry_Pi_5.GPIO21, J3.GPIO_21
  N90: Raspberry_Pi_5.GPIO20, J3.GPIO_20
  N91: Raspberry_Pi_5.GPIO16, J3.GPIO_16
  N92: Raspberry_Pi_5.GPIO12, J3.GPIO_12
  N93: Raspberry_Pi_5.ID_SC, J3.ID_SC
  N94: Raspberry_Pi_5.GPIO7, J3.GPIO_7
  N95: Raspberry_Pi_5.GPIO8, J3.GPIO_8
  N96: Raspberry_Pi_5.GPIO25, J3.GPIO_25
  N97: Raspberry_Pi_5.GPIO24, J3.GPIO_24
  N98: Raspberry_Pi_5.GPIO23, J3.GPIO_23
  N99: Raspberry_Pi_5.GPIO18, J3.GPIO_18
  N100: Raspberry_Pi_5.GPIO15, J3.GPIO_15
  N101: Raspberry_Pi_5.GPIO14, J3.GPIO_14
  5V_3: Raspberry_Pi_5.5V, J3.5V
  N102: J3.SDA, Part3.SDA
  N103: J3.SCL, Part3.SCL
  N104: J3.3.3V#16, Part3.VCC

notes:
  LED
  IR LED
  LASER MODULE

custom parts:
  T Cobbler Plus: The T-Cobbler Plus is an add on prototyping board from Adafruit specifically designed for the Raspberry Pi B+ that can break out all those tasty power, GPIO, I2C and SPI pins from the 40-pin header onto a solderless breadboard. This set will make "cobbling together" prototypes with the Pi super easy. The T-Cobbler Plus can plug into any solderless breadboard.
  Raspberry Pi 4: The RPi4, a faster version of the awesome Raspberry Pi 2 B ARM Board with 40 pin gpio. Ready for special Raspberry Pi B+ and RPi2 Hat (Hardware attached (on) top)
  KY-008 Laser Transmitter Module: KY-008 Laser Transmitter Module, emits a dot shaped red laser beam.
  Adafruit TSL2591 High Dynamic Range Digital Light Sensor: When the future is dazzlingly-bright, this ultra-high-range luminosity sensor will help you measure it. The TSL2591 luminosity sensor is an advanced digital light sensor, ideal for use in a wide range of light situations. Compared to low cost CdS cells, this sensor is more precise, allowing for exact lux calculations and can be configured for different gain/timing ranges to detect light ranges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
